# Fritzing sketch schematic (saved by Fritzing 0.9.6b)
breadboards: 1

parts:
  Q1 = MOSFET-NCHANNEL [package=to220v]
  J1 = Piezo Speaker
  VCC1 = Battery block 9V
  Part1 = Arduino Uno (Rev3)
  R1 = Resistor [tolerance=±5% power=0.25 resistance=150 package=THT]
  R2 = Resistor [tolerance=±5% power=0.25 resistance=10000 package=THT]

nets:
  N1: Q1.G, Part1.D5_PWM, R1.Pin_0, R1.Pin_1, R2.Pin_0
  N2: Q1.D, J1.pin1
  GND: Q1.S, J1.pin2, VCC1.-, VCC1.+, Part1.GND, Part1.VIN, R2.Pin_1
